# Fritzing sketch Tomo 11 Viendo con Sonido - Sensor Ultrasónico HC-SR04 (saved by Fritzing 0.9.3b)
breadboards: 1

parts:
  Display1 = LCD screen 16x2 IIC [part_number=101290]
  Componente2 = Arduino Uno (Rev3) [part_number=1]
  U1 = LM2596 step down module
  JACK1 = 2.1mm Barrel Jack with Terminal Block
  J1 = Basic Servo
  D1 = LED_BARGRAPH_10 [package=led_bargaph_8]
  R2 = Resistor [tolerance=±5% resistance=220 package=THT]
  R3 = Resistor [tolerance=±5% resistance=220 package=THT]
  R4 = Resistor [tolerance=±5% resistance=220 package=THT]
  R5 = Resistor [tolerance=±5% resistance=220 package=THT]
  R6 = Resistor [tolerance=±5% resistance=220 package=THT]
  R7 = Resistor [tolerance=±5% resistance=220 package=THT]
  R8 = Resistor [tolerance=±5% resistance=220 package=THT]
  R9 = Resistor [tolerance=±5% resistance=220 package=THT]
  Componente3 = HC-SR04

nets:
  GND: Display1.GND, Componente2.GND, U1.IN-, U1.OUT-, JACK1.NEG, J1.gnd, R2.Pin_0, R3.Pin_1, R4.Pin_1, R5.Pin_1, R6.Pin_1, R7.Pin_1, R8.Pin_1, R9.Pin_1, Componente3.Gnd
  VCC: Display1.VCC, Componente2.5V, Componente3.Vcc
  N1: Display1.SDA, Componente2.A4/SDA
  N2: Display1.SCL, Componente2.A5/SCL
  N3: Componente2.D8, D1.F_A
  N4: Componente2.D9_PWM, D1.E_A
  N5: Componente2.D10_PWM/SS, D1.D_A
  N6: Componente2.D11_PWM/MOSI, D1.C_A
  N7: Componente2.D12/MISO, D1.B_A
  N8: Componente2.D13/SCK, D1.A_A
  N9: Componente2.D2, Componente3.Echo
  N10: Componente2.D3_PWM, Componente3.Trig
  N11: Componente2.D5_PWM, J1.pulse
  N12: Componente2.D6_PWM, D1.H_A
  N13: Componente2.D7, D1.G_A
  N14: U1.IN+, JACK1.POS
  N15: U1.OUT+, J1.vcc
  N16: D1.H_C, R2.Pin_1
  N17: D1.G_C, R9.Pin_0
  N18: D1.F_C, R8.Pin_0
  N19: D1.E_C, R7.Pin_0
  N20: D1.D_C, R6.Pin_0
  N21: D1.C_C, R3.Pin_0
  N22: D1.B_C, R5.Pin_0
  N23: D1.A_C, R4.Pin_0

notes:
  REGULADA A 5V

custom parts:
  LCD screen 16x2 IIC: LCD screen with HD44780 controller enables showing text, symbols, value or anything else that comes from Croduino/Arduino. It is capable of showing 16 symbols in two lines and therefore can be used in many projects that need to send clearly visible and legible output information.. • Color of symbols: White • Backlight: Blue • Dimensions: 80 x 36 x 12 mm • Screen dimensions: 64.5 x 16 mm •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
  LM2596 step down module: LM2596 DC-DC step down power supply module 3 A.
  LED_BARGRAPH_10: 8-Segment LED Bar Graph
  HC-SR04: HC-SR04 ultrasonic distance sensor

// code stored in the sketch: tomo_9_el_panorama_completo_dht11_rel_s_y_lcd1.ino
/*
 * Misión 09: El Panorama Completo
 * Descripción: Muestra Temp/Humedad del DHT11 en una LCD y activa un relé.
 * Por: Profe Campos
 * CECyTEM 05 Guacamayas
*/

// --- INCLUIR LIBRERÍAS ---
#include <Wire.h>
#include <LiquidCrystal_I2C.h> // Para la pantalla LCD
#include "DHT.h"                 // Para el sensor DHT

// --- CONFIGURACIÓN DE COMPONENTES ---
#define DHTPIN 2       // Pin donde está el DHT11
#define DHTTYPE DHT11  // Definimos que es un DHT11
const int pinRele = 7; // Pin para controlar el relé

// Inicializamos los objetos
DHT dht(DHTPIN, DHTTYPE);
LiquidCrystal_I2C lcd(0x27, 16, 2); // Dirección I2C, 16 columnas, 2 filas

void setup() {
  Serial.begin(9600);
  pinMode(pinRele, OUTPUT);
  digitalWrite(pinRele, LOW); // Nos aseguramos que el relé empiece apagado

  dht.begin(); // Iniciamos el sensor DHT
  
  lcd.init();      // Iniciamos la pantalla LCD
  lcd.backlight(); // Encendemos la luz de fondo
  lcd.setCursor(0, 0); // Ponemos el cursor en la columna 0, fila 0
  lcd.print("Estacion CTEC");
  lcd.setCursor(0, 1); // Columna 0, fila 1
  lcd.print("Iniciando...");
  delay(2000);
  lcd.clear(); // Limpiamos la pantalla
}

void loop() {
  delay(2000); // Esperamos 2 segundos entre lecturas

  // Leer la humedad y la temperatura toma unos 250ms
  float h = dht.readHumidity();
  float t = dht.readTemperature();

  // Verificamos si la lectura falló (muy común con los DHT)
  if (isnan(h) || isnan(t)) {
    Serial.println("Error al leer del sensor DHT!");
    lcd.setCursor(0, 0);
    lcd.print("Error de Sensor");
    return; // Salimos del loop y lo intentamos de nuevo
  }

  // --- MOSTRAMOS EN LCD ---
  lcd.setCursor(0, 0);
  lcd.print("Temp: ");
  lcd.print(t);
  lcd.print(" C");

  lcd.setCursor(0, 1);
  lcd.print("Hum:  ");
  lcd.print(h);
  lcd.print(" %");

  // --- LÓGICA DEL RELÉ ---
  if (t > 30.0) { // Si la temperatura supera los 30 grados
    digitalWrite(pinRele, HIGH); // Activamos el relé
  } else {
    digitalWrite(pinRele, LOW);  // Lo desactivamos
  }
}
