# Fritzing sketch Tomo 13 Estación de Monitoreo Ambiental y Radar Gráfico (saved by Fritzing 0.9.3b)
circuit board: 8.46667cm x 5.64444cm
breadboards: 1

parts:
  Componente2 = Arduino Uno (Rev3) [part_number=1]
  Componente4 = Black Joystick KY-023
  OLED1 = SSD1306 0.96in 128x64 I2C Monochrome OLED Display
  DS1 = DS18B20 1-Wire Temperature Sensor Probe
  R1 = Resistor [tolerance=±5% resistance=4.7k package=THT]
  SG1 = Buzzer 12mm [part_number=COM-07950 package=buzzer-12mm-ns]
  J1 = Basic Servo
  Componente5 = HC-SR04
  U1 = LM2596 step down module
  JACK1 = 2.1mm Barrel Jack with Terminal Block

nets:
  N1: Componente2.A0, Componente4.VRy
  N2: Componente2.A4/SDA, OLED1.SDA
  N3: Componente2.A5/SCL, OLED1.SCL
  N4: Componente2.D9_PWM, Componente5.Trig
  N5: Componente2.D10_PWM/SS, Componente5.Echo
  GND: Componente2.GND, Componente4.GND, OLED1.GND, DS1.GND, SG1.2, J1.gnd, Componente5.Gnd, U1.IN-, U1.OUT-, JACK1.NEG
  N6: Componente2.D2, DS1.DQ, R1.Pin_1
  N7: Componente2.D3_PWM, Componente4.SW
  N8: Componente2.D6_PWM, J1.pulse
  VCC: Componente2.5V, Componente4.+5V, OLED1.VCC, DS1.VDD, R1.Pin_0, Componente5.Vcc
  N9: J1.vcc, U1.OUT+
  N10: U1.IN+, JACK1.POS

custom parts:
  Black Joystick KY-023: Description: The joystick is a combination of 2 analoog potentiometer and a digital switch. Arduino GND --> Module pin - Arduino +5V --> Module pin +5V Arduino Analoog 0 --> Module VRx Arduino Analoog 1 --> Module VRy Arduino Digital --> Module SW Dimensions: 1" x 1.25"
  Buzzer 12mm: Buzzer 12mm Spark Fun Electronics SKU : Comp-Buzzer Through hole This is a small 12mm round speaker that operates around the audible 2kHz range. You can use these speakers to create simple music or user interfaces. This is not a true piezoelectric speaker but behaves similarly. Instead of a piezoelectric crystal that vibrates with an electric current, this tiny speaker uses an electromagnet to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
  HC-SR04: HC-SR04 ultrasonic distance sensor
  LM2596 step down module: LM2596 DC-DC step down power supply module 3 A.

// code stored in the sketch: tomo_9_el_panorama_completo_dht11_rel_s_y_lcd1.ino
/*
 * Misión 09: El Panorama Completo
 * Descripción: Muestra Temp/Humedad del DHT11 en una LCD y activa un relé.
 * Por: Profe Campos
 * CECyTEM 05 Guacamayas
*/

// --- INCLUIR LIBRERÍAS ---
#include <Wire.h>
#include <LiquidCrystal_I2C.h> // Para la pantalla LCD
#include "DHT.h"                 // Para el sensor DHT

// --- CONFIGURACIÓN DE COMPONENTES ---
#define DHTPIN 2       // Pin donde está el DHT11
#define DHTTYPE DHT11  // Definimos que es un DHT11
const int pinRele = 7; // Pin para controlar el relé

// Inicializamos los objetos
DHT dht(DHTPIN, DHTTYPE);
LiquidCrystal_I2C lcd(0x27, 16, 2); // Dirección I2C, 16 columnas, 2 filas

void setup() {
  Serial.begin(9600);
  pinMode(pinRele, OUTPUT);
  digitalWrite(pinRele, LOW); // Nos aseguramos que el relé empiece apagado

  dht.begin(); // Iniciamos el sensor DHT
  
  lcd.init();      // Iniciamos la pantalla LCD
  lcd.backlight(); // Encendemos la luz de fondo
  lcd.setCursor(0, 0); // Ponemos el cursor en la columna 0, fila 0
  lcd.print("Estacion CTEC");
  lcd.setCursor(0, 1); // Columna 0, fila 1
  lcd.print("Iniciando...");
  delay(2000);
  lcd.clear(); // Limpiamos la pantalla
}

void loop() {
  delay(2000); // Esperamos 2 segundos entre lecturas

  // Leer la humedad y la temperatura toma unos 250ms
  float h = dht.readHumidity();
  float t = dht.readTemperature();

  // Verificamos si la lectura falló (muy común con los DHT)
  if (isnan(h) || isnan(t)) {
    Serial.println("Error al leer del sensor DHT!");
    lcd.setCursor(0, 0);
    lcd.print("Error de Sensor");
    return; // Salimos del loop y lo intentamos de nuevo
  }

  // --- MOSTRAMOS EN LCD ---
  lcd.setCursor(0, 0);
  lcd.print("Temp: ");
  lcd.print(t);
  lcd.print(" C");

  lcd.setCursor(0, 1);
  lcd.print("Hum:  ");
  lcd.print(h);
  lcd.print(" %");

  // --- LÓGICA DEL RELÉ ---
  if (t > 30.0) { // Si la temperatura supera los 30 grados
    digitalWrite(pinRele, HIGH); // Activamos el relé
  } else {
    digitalWrite(pinRele, LOW);  // Lo desactivamos
  }
}
